// Logisim project CPU2.circ as structural Verilog: 12 circuits, main circuit mboard
module mboard (
);

  wire and_1_out, and_2_out, and_3_out, and_4_out, clock_1_out, cpu_1_oe, cpu_1_we;
  wire [7:0] cpu_1_dout, ram_1_data, rom_1_data;
  wire [15:0] cpu_1_addr;

  cpu cpu_1 (
    .CLK(clock_1_out), .DIN(cpu_1_dout), .OE(cpu_1_oe), .WE(cpu_1_we), .DOUT(cpu_1_dout), .ADDR(cpu_1_addr));  // open: INT
  Clock clock_1 (.out(clock_1_out));
  // Probe on cpu_1_dout
  // Probe on cpu_1_addr
  Pull_Resistor pull_resistor_1 (.node(cpu_1_addr));
  and and_1 (and_1_out, ~cpu_1_addr[14], ~cpu_1_addr[15]);  // AND_Gate
  and and_2 (and_2_out, and_1_out, cpu_1_oe, ~cpu_1_we);  // AND_Gate
  and and_3 (and_3_out, and_1_out, ~cpu_1_oe, cpu_1_we);  // AND_Gate
  assign cpu_1_dout = and_2_out ? ram_1_data : 8'bz;  // Controlled_Buffer controlled_buffer_1
  RAM #(.addrWidth(14), .databus("bidir"), .enables("line")) ram_1 (
    .addr(cpu_1_addr[13:0]), .data(ram_1_data));  // open: we, oe, clk
  assign ram_1_data = and_3_out ? cpu_1_dout : 8'bz;  // Controlled_Buffer controlled_buffer_2
  ROM #(.addrWidth(14)) rom_1 (.addr(cpu_1_addr[13:0]), .data(rom_1_data));
  and and_4 (and_4_out, cpu_1_addr[14], cpu_1_addr[15]);
  assign cpu_1_dout = and_4_out ? rom_1_data : 8'bz;  // Controlled_Buffer controlled_buffer_3

  // Notes on the sheet:
  //   contents of rom_1 (hex, n*v repeats v):
  //   16382*0 80
endmodule

module cpu (
  input  CLK,
  input  [7:0] DIN,
  input  INT,
  output [7:0] DOUT,
  output WE,
  output OE,
  output [15:0] ADDR
);

  wire AB_sh, AB_sl, CD_sh, CD_sl;
  wire [0:0] CTRL_out_6;
  wire [2:0] CTRL_mm, CTRL_out_6_2, CTRL_pc, CTRL_sp;
  wire [3:0] alu_1_z, CTRL_ab, CTRL_cd;
  wire [5:0] CTRL_alu;
  wire [7:0] AB_tohigh, AB_tolow, CD_tohigh, CD_tolow, CTRL_inr, multiplexer_2_out, register_1_q,
       register_2_q, register_3_q, register_4_q;
  wire [15:0] mm_circ_1_out_7, MM_out_7, PC_out_5, SP_out_5;

  MM_CIRC mm_circ_1 (.out_7(mm_circ_1_out_7));  // open: in_4, in_1, in_2, in_3, out_5, out_6
  // Probe on mm_circ_1_out_7
  assign ADDR = CTRL_out_6[0] ? {{13{1'b1}}, CTRL_out_6_2} : 16'bz;  // Controlled_Buffer controlled_buffer_1
  // Probe on CTRL_inr
  // Probe on multiplexer_2_out
  Multiplexer #(.disabled("Z"), .width(8)) multiplexer_1 (.in1(multiplexer_2_out), .out(DOUT), .sel(WE));  // open: in0
  Multiplexer #(.disabled("Z"), .width(8)) multiplexer_2 (.in1(DIN), .out(multiplexer_2_out), .sel(OE));  // open: in0
  // Probe on CTRL_cd
  // Probe on CTRL_ab
  CTRL_CIRC CTRL (
    .Clk(CLK), .DATABUS(multiplexer_2_out), .FLAG(alu_1_z), .INT(INT), .PC(CTRL_pc), .SP(CTRL_sp),
    .MM(CTRL_mm), .CD(CTRL_cd), .AB(CTRL_ab), .ALU(CTRL_alu), .INR(CTRL_inr),
    .out_6({CTRL_out_6_2, CTRL_out_6[0]}), .ADR({OE, WE}));  // open: in_2
  PC_CIRC PC (.in_1(ADDR), .in_3(CTRL_pc), .in_2(CLK), .out_4(ADDR), .out_5(PC_out_5));
  // Probe on PC_out_5
  SP_CIRC SP (.in_1(ADDR), .in_3(CTRL_sp), .in_2(CLK), .out_4(ADDR), .out_5(SP_out_5));
  // Probe on SP_out_5
  MM_CIRC MM (
    .in_4(CTRL_mm), .in_1(ADDR), .in_2(multiplexer_2_out), .in_3(CLK), .out_5(multiplexer_2_out),
    .out_6(ADDR), .out_7(MM_out_7));
  // Probe on MM_out_7
  Register register_1 (.D(CD_tolow), .en(CD_sl), .Q(register_1_q), .clk(CLK));  // open: clr
  Register register_2 (.D(AB_tolow), .en(AB_sl), .Q(register_2_q), .clk(CLK));  // open: clr
  // Probe on ADDR
  REG_CRTL CD (
    .In8(multiplexer_2_out), .in_2(CTRL_cd), .FromLow(register_1_q), .FromHigh(register_3_q), .SH(CD_sh),
    .Out8(multiplexer_2_out), .SL(CD_sl), .ToLow(CD_tolow), .ToHigh(CD_tohigh));
  Register register_3 (.D(CD_tohigh), .en(CD_sh), .Q(register_3_q), .clk(CLK));  // open: clr
  REG_CRTL AB (
    .In8(multiplexer_2_out), .in_2(CTRL_ab), .FromLow(register_2_q), .FromHigh(register_4_q), .SH(AB_sh),
    .Out8(multiplexer_2_out), .SL(AB_sl), .ToLow(AB_tolow), .ToHigh(AB_tohigh));
  Register register_4 (.D(AB_tohigh), .en(AB_sh), .Q(register_4_q), .clk(CLK));  // open: clr
  ALU alu_1 (
    .A(register_2_q), .B(register_4_q), .cin(CTRL_alu[5]), .op3(CTRL_alu[4]), .op2(CTRL_alu[3]),
    .op1(CTRL_alu[2]), .op0(CTRL_alu[1]), .X(CTRL_alu[0]), .O(multiplexer_2_out), .Z(alu_1_z[0]),
    .G(alu_1_z[1]), .E(alu_1_z[2]), .C(alu_1_z[3]));
endmodule

module ALU (
  input  [7:0] A,
  input  [7:0] B,
  input  cin,
  input  op3,
  input  op2,
  input  op1,
  input  op0,
  input  X,
  output [7:0] O,
  output Z,
  output G,
  output E,
  output C
);

  wire adder_1_cout, subtractor_1_bout;
  wire [7:0] adder_1_out, and_1_out, demultiplexer_1_out0, demultiplexer_1_out1, demultiplexer_1_out2,
       demultiplexer_1_out3, demultiplexer_1_out4, demultiplexer_1_out5, demultiplexer_1_out6,
       demultiplexer_1_out7, demultiplexer_2_out0, demultiplexer_2_out1, demultiplexer_2_out2,
       demultiplexer_2_out3, demultiplexer_2_out4, demultiplexer_2_out6, demultiplexer_2_out7, not_1_out,
       or_1_out, shifter_1_out, shifter_2_out, subtractor_1_out, xor_1_out;

  Demultiplexer #(.select(3), .width(8)) demultiplexer_1 (
    .out0(demultiplexer_1_out0), .out1(demultiplexer_1_out1), .out2(demultiplexer_1_out2),
    .out3(demultiplexer_1_out3), .out4(demultiplexer_1_out4), .out5(demultiplexer_1_out5),
    .out6(demultiplexer_1_out6), .out7(demultiplexer_1_out7), .in(A), .sel({op2, op1, op0}));
  Demultiplexer #(.select(3), .width(8)) demultiplexer_2 (
    .out0(demultiplexer_2_out0), .out1(demultiplexer_2_out1), .out2(demultiplexer_2_out2),
    .out3(demultiplexer_2_out3), .out4(demultiplexer_2_out4), .out6(demultiplexer_2_out6),
    .out7(demultiplexer_2_out7), .in(B), .sel({op2, op1, op0}));  // open: out5
  Adder adder_1 (.a(demultiplexer_1_out0), .b(demultiplexer_2_out0), .out(adder_1_out), .cin(cin), .cout(adder_1_cout));
  Subtractor subtractor_1 (
    .a(demultiplexer_1_out1), .b(demultiplexer_2_out1), .out(subtractor_1_out), .bin(cin),
    .bout(subtractor_1_bout));
  assign and_1_out = demultiplexer_1_out2 & demultiplexer_2_out2;  // AND_Gate and_1, 8 bits wide
  assign or_1_out = demultiplexer_1_out3 | demultiplexer_2_out3;  // OR_Gate or_1, 8 bits wide
  assign xor_1_out = demultiplexer_1_out4 ^ demultiplexer_2_out4;  // XOR_Gate xor_1, 8 bits wide
  assign not_1_out = ~demultiplexer_1_out5;  // NOT_Gate not_1, 8 bits wide
  Shifter #(.shift("rl")) shifter_1 (
    .in(demultiplexer_1_out6), .\dist (demultiplexer_2_out6[2:0]), .out(shifter_1_out));
  Shifter #(.shift("rr")) shifter_2 (
    .in(demultiplexer_1_out7), .\dist (demultiplexer_2_out7[2:0]), .out(shifter_2_out));
  Multiplexer #(.disabled("Z"), .enable("true"), .select(3), .width(8)) multiplexer_1 (
    .in0(adder_1_out), .in1(subtractor_1_out), .in2(and_1_out), .in3(or_1_out), .in4(xor_1_out),
    .in5(not_1_out), .in6(shifter_1_out), .in7(shifter_2_out), .out(O), .sel({op2, op1, op0}), .en(X));
  nor nor_1 (Z, A[0], A[1], A[2], A[3], A[4], A[5], A[6], A[7]);
  Comparator comparator_1 (.a(A), .b(B), .gt(G), .eq(E));  // open: lt
  or or_2 (C, adder_1_cout, subtractor_1_bout);

  // Notes on the sheet:
  //   A: pull=down
  //   B: pull=down
endmodule

module CTRL_CIRC (
  input  INT,
  input  [15:0] in_2,
  input  Clk,
  input  [7:0] DATABUS,
  input  [3:0] FLAG,
  output [3:0] out_6,
  output [1:0] ADR,
  output [2:0] PC,
  output [2:0] SP,
  output [2:0] MM,
  output [3:0] CD,
  output [3:0] AB,
  output [5:0] ALU,
  output [7:0] INR
);

  wire and_1_out, j_k_ff_1_q, j_k_ff_1_qn;
  wire [2:0] counter_1_q, multiplexer_2_out;
  wire [3:0] and_2_out, decoder_1_out0, pull_resistor_4_node, register_2_q, t_ff_1_q;
  wire [11:11] or_1_out;
  wire [15:0] rom_1_data;
  wire [31:0] pull_resistor_5_node, rom_2_data;
  wire [31:28] multiplexer_2_out_2;

  // Probe on in_2
  Pull_Resistor pull_resistor_1 ();  // open: node
  and and_1 (and_1_out, multiplexer_2_out[0], INT);
  Register register_1 (.D(DATABUS), .en(multiplexer_2_out[1]), .Q(INR), .clk(Clk));  // open: clr
  Register #(.width(4)) register_2 (.D(FLAG), .en(multiplexer_2_out[2]), .Q(register_2_q), .clk(Clk));  // open: clr
  T_Flip_Flop #(.trigger("falling")) t_ff_1 (.clk(Clk), .T(j_k_ff_1_qn), .Q(t_ff_1_q[0]));  // open: Qn, preset, reset
  J_K_Flip_Flop #(.trigger("falling")) j_k_ff_1 (
    .J(rom_1_data[0]), .clk(Clk), .K(and_1_out), .Q(j_k_ff_1_q), .Qn(j_k_ff_1_qn));  // open: preset, reset
  Decoder #(.enable("false"), .select(2)) decoder_1 (
    .out0(decoder_1_out0[0]), .out1(decoder_1_out0[1]), .out2(decoder_1_out0[2]), .out3(decoder_1_out0[3]),
    .sel(INR[1:0]));
  Counter #(.max('h7), .trigger("falling"), .width(3)) counter_1 (
    .count(j_k_ff_1_q), .Q(counter_1_q), .up(j_k_ff_1_q), .clk(Clk));  // open: load, D, carry, clr
  assign and_2_out = decoder_1_out0 & register_2_q;  // AND_Gate and_2, 4 bits wide
  or or_1 (or_1_out[11], and_2_out[0], and_2_out[1], and_2_out[2], and_2_out[3]);
  ROM #(.addrWidth(4), .dataWidth(16)) rom_1 (.addr({{2{t_ff_1_q[3]}}, INT, t_ff_1_q[0]}), .data(rom_1_data));
  Pull_Resistor pull_resistor_2 (.node(t_ff_1_q[3]));
  ROM #(.addrWidth(12), .dataWidth(32)) rom_2 (.addr({or_1_out[11], INR, counter_1_q}), .data(rom_2_data));
  Pull_Resistor pull_resistor_3 (.node(rom_2_data));
  Pull_Resistor pull_resistor_4 (.node(pull_resistor_4_node));
  Multiplexer #(.width(4)) multiplexer_1 (
    .in0(rom_1_data[15:12]), .in1(pull_resistor_4_node), .out(out_6), .sel(j_k_ff_1_q));
  Pull_Resistor pull_resistor_5 (.node({pull_resistor_5_node[31:26], rom_1_data[3:2], rom_1_data[7:4], rom_1_data[11:8], pull_resistor_5_node[15:0]}));
  Multiplexer #(.width(32)) multiplexer_2 (
    .in0({pull_resistor_5_node[31:26], rom_1_data[3:2], rom_1_data[7:4], rom_1_data[11:8], pull_resistor_5_node[15:0]}),
    .in1(rom_2_data), .out({multiplexer_2_out_2, multiplexer_2_out, ADR, PC, SP, MM, CD, AB, ALU}),
    .sel(j_k_ff_1_q));
  Pull_Resistor pull_resistor_6 ();  // open: node

  // Notes on the sheet:
  //   Clk: pull=down
  //   contents of rom_1 (hex, n*v repeats v):
  //   d010 f011 9010 b010
  //   contents of rom_2 (hex, n*v repeats v):
  //   aa00000 4000000 6*0 aa00000 7*0 aa00000 7*0 aa00000 7*0 aa00000 7*0 aa00000 7*0 aa00000 7*0 aa00000
  //   7*0 aa00000 4000000 6*0 aa00000 7*0 aa00000 7*0 aa00000 7*0 aa00000 7*0 aa00000 7*0 aa00000 7*0
  //   aa00000 7*0 aa00000 2a00100 4000000 5*0 aa00000 2a00200 4000000 5*0 aa00000 7*0 aa00000 7*0 aa00000
  //   7*0 aa00000 7*0 aa00000 7*0 aa00000 7*0 aa00000 7*0 aa00000 7*0 aa00000 7*0 aa00000 7*0 aa00000 7*0
  //   aa00000 7*0 aa00000 7*0 aa00000 7*0 aa00000 7*0 aa00000 7*0 aa00000 7*0 aa00000 7*0 aa00000 7*0
  //   aa00000 7*0 aa00000 7*0 aa00000 7*0 aa00000 7*0 aa00000 7*0 aa00000 7*0 aa00000 7*0 aa00000 7*0
  //   aa00000 7*0 aa00000 7*0 aa00000 7*0 aa00000 7*0 aa00000 7*0 aa00000 7*0 aa00000 7*0 aa00000 7*0
  //   aa00000 7*0 aa00000 7*0 aa00000 7*0 aa00000 7*0 aa00000 7*0 aa00000 7*0 aa00000 7*0 aa00000 7*0
  //   aa00000 7*0 aa00000 7*0 aa00000 7*0 aa00000 7*0 aa00000 7*0 aa00000 7*0 aa00000 7*0 aa00000 7*0
  //   aa00000 7*0 aa00000 7*0 aa00000 7*0 aa00000 7*0 aa00000 7*0 aa00000 7*0 aa00000 7*0 aa00000 7*0
  //   aa00000 7*0 aa00000 7*0 aa00000 7*0 aa00000 7*0 aa00000 7*0 aa00000 7*0 aa00000 7*0 aa00000 7*0
  //   aa00000 7*0 aa00000 7*0 aa00000 7*0 aa00000 7*0 aa00000 7*0 aa00000 7*0 aa00000 7*0 aa00000 7*0
  //   aa00000 7*0 aa00000 7*0 aa00000 7*0 aa00000 7*0 aa00000 7*0 aa00000 7*0 aa00000 7*0 aa00000 7*0
  //   aa00000 7*0 aa00000 7*0 aa00000 7*0 aa00000 7*0 aa00000 7*0 aa00000 7*0 aa00000 7*0 aa00000 7*0
  //   aa00000 7*0 aa00000 7*0 aa00000 7*0 aa00000 7*0 aa00000 7*0 aa00000 7*0 aa00000 7*0 aa00000 7*0
  //   aa00000 7*0 aa00000 7*0 aa00000 7*0 aa00000 7*0 aa00000 7*0 aa00000 7*0 aa00000 7*0 aa00000 7*0
  //   aa00000 7*0 aa00000 7*0 aa00000 7*0 aa00000 7*0 aa00000 7*0 aa00000 7*0 aa00000 7*0 aa00000 7*0
  //   aa00000 7*0 aa00000 7*0 aa00000 7*0 aa00000 7*0 aa00000 7*0 aa00000 7*0 aa00000 7*0 aa00000 7*0
  //   aa00000 7*0 aa00000 7*0 aa00000 7*0 aa00000 7*0 aa00000 7*0 aa00000 7*0 aa00000 7*0 aa00000 7*0
  //   aa00000 7*0 aa00000 7*0 aa00000 7*0 aa00000 7*0 aa00000 7*0 aa00000 7*0 aa00000 7*0 aa00000 7*0
  //   aa00000 7*0 aa00000 7*0 aa00000 7*0 aa00000 7*0 aa00000 7*0 aa00000 7*0 aa00000 7*0 aa00000 7*0
  //   aa00000 7*0 aa00000 7*0 aa00000 7*0 aa00000 7*0 aa00000 7*0 aa00000 7*0 aa00000 7*0 aa00000 7*0
  //   aa00000 7*0 aa00000 7*0 aa00000 7*0 aa00000 7*0 aa00000 7*0 aa00000 7*0 aa00000 7*0 aa00000 7*0
  //   aa00000 7*0 aa00000 7*0 aa00000 7*0 aa00000 7*0 aa00000 7*0 aa00000 7*0 aa00000 7*0 aa00000 7*0
  //   aa00000 7*0 aa00000 7*0 aa00000 7*0 aa00000 7*0 aa00000 7*0 aa00000 7*0 aa00000 7*0 aa00000 7*0
  //   aa00000 7*0 aa00000 7*0 aa00000 7*0 aa00000 7*0 aa00000 7*0 aa00000 7*0 aa00000 7*0 aa00000 7*0
  //   aa00000 7*0 aa00000 7*0 aa00000 7*0 aa00000 7*0 aa00000 7*0 aa00000 7*0 aa00000 7*0 aa00000 7*0
  //   aa00000 7*0 aa00000 7*0 aa00000 7*0 aa00000 7*0 aa00000 7*0 aa00000 7*0 aa00000 7*0 aa00000 7*0
  //   aa00000 7*0 aa00000 7*0 aa00000 7*0 aa00000 7*0 aa00000 7*0 aa00000 7*0 aa00000 7*0 aa00000 7*0
  //   aa00000 7*0 aa00000 7*0 aa00000 7*0 aa00000 7*0 aa00000 7*0 aa00000 7*0 aa00000 7*0 aa00000 7*0
  //   aa00000 7*0 aa00000 7*0 aa00000 7*0 aa00000 7*0 aa00000 7*0 aa00000 7*0 aa00000 7*0 aa00000 7*0
  //   aa00000 7*0 aa00000 7*0 aa00000 7*0 aa00000 7*0 aa00000 7*0 aa00000 7*0 aa00000 7*0 aa00000 7*0
  //   aa00000 7*0 aa00000 7*0 aa00000
endmodule

module bboard (
);

  wire clock_1_out, t_ff_1_q;

  Clock clock_1 (.out(clock_1_out));
  T_Flip_Flop t_ff_1 (.clk(clock_1_out), .Q(t_ff_1_q));  // open: T, Qn, preset, reset
  T_Flip_Flop t_ff_2 (.clk(clock_1_out), .T(t_ff_1_q));  // open: Q, Qn, preset, reset
endmodule

module REG_CRTL (
  input  [7:0] In8,
  input  [3:0] in_2,
  input  [7:0] FromLow,
  input  [7:0] FromHigh,
  output [7:0] Out8,
  output SH,
  output SL,
  output [7:0] ToLow,
  output [7:0] ToHigh
);

  Multiplexer #(.disabled("Z"), .enable("true"), .width(8)) multiplexer_1 (
    .in0(FromLow), .in1(FromHigh), .out(Out8), .sel(in_2[0]), .en(in_2[1]));

  assign SH = in_2[3];
  assign SL = in_2[2];
  assign ToHigh = In8;
  assign ToLow = In8;
endmodule

module CNTR_CTRL (
  input  [7:0] olow,
  input  [7:0] ohi,
  input  [3:0] in_3,
  output [15:0] out16,
  output [7:0] out8,
  output idh,
  output idl,
  output ldh,
  output ldl,
  output ct
);

  wire and_1_out, and_2_out;

  and and_1 (and_1_out, in_3[3], in_3[2]);
  and and_2 (and_2_out, ~in_3[3], in_3[2]);  // AND_Gate
  Multiplexer #(.disabled("Z"), .enable("true"), .width(8)) multiplexer_1 (
    .in0(olow), .in1(ohi), .out(out8), .sel(and_1_out), .en(in_3[3]));
  and and_3 (idh, in_3[1], ~in_3[0]);  // AND_Gate
  and and_4 (ldh, ~in_3[1], in_3[0]);  // AND_Gate
  assign out16 = and_2_out ? {ohi, olow} : 16'bz;  // Controlled_Buffer controlled_buffer_1

  assign ct = in_3[1];
  assign idl = idh;
  assign ldl = ldh;
endmodule

module ADR_CTRL (
  input  [7:0] SHFL,
  input  [7:0] SHFH,
  input  [1:0] in_3,
  output [15:0] out_4,
  output out_5,
  output out_6
);

  assign out_4 = in_3[1] ? {SHFH, SHFL} : 16'bz;  // Controlled_Buffer controlled_buffer_1

  assign out_5 = in_3[0];
  assign out_6 = in_3[0];
endmodule

module NCNTR (
  input  [15:0] in_1,
  input  [7:0] in_2,
  input  [3:0] in_3,
  output [15:0] out_4,
  output [7:0] out_5
);

  wire and_1_out, counter_1_carry, counter_3_carry, decoder_1_out2, decoder_1_out3, or_1_out;
  wire [2:2] decoder_1_out1;
  wire [7:0] counter_1_q, counter_3_q, multiplexer_1_out, multiplexer_2_out, pla_1_out;

  PLA pla_1 (.in(in_3), .out(pla_1_out));
  Multiplexer #(.width(8)) multiplexer_1 (.in0(in_2), .in1(in_1[7:0]), .out(multiplexer_1_out), .sel(pla_1_out[7]));
  Multiplexer #(.width(8)) multiplexer_2 (.in0(in_2), .in1(in_1[15:8]), .out(multiplexer_2_out), .sel(pla_1_out[7]));
  Decoder #(.enable("false"), .select(2)) decoder_1 (
    .out1(decoder_1_out1[2]), .out2(decoder_1_out2), .out3(decoder_1_out3), .sel(in_3[1:0]));  // open: out0
  Decoder #(.enable("false"), .select(3)) decoder_2 (.sel({decoder_1_out1[2], in_3[3:2]}));  // open: out0, out1, out2, out3, out4, out5, out6, out7
  Counter counter_1 (
    .load(pla_1_out[1]), .D(multiplexer_1_out), .count(pla_1_out[0]), .Q(counter_1_q),
    .carry(counter_1_carry), .up(pla_1_out[2]));  // open: clk, clr
  or or_1 (or_1_out, decoder_1_out3, decoder_1_out2);
  and and_1 (and_1_out, counter_1_carry, pla_1_out[0]);
  Counter counter_2 (.count(or_1_out), .up(decoder_1_out3));  // open: load, D, Q, carry, clk, clr
  Counter counter_3 (
    .load(pla_1_out[3]), .D(multiplexer_2_out), .count(and_1_out), .Q(counter_3_q), .carry(counter_3_carry),
    .up(pla_1_out[2]));  // open: clk, clr
  Counter counter_4 (.count(or_1_out), .up(decoder_1_out3));  // open: load, D, Q, carry, clk, clr
  assign out_4 = pla_1_out[4] ? {counter_3_q, counter_1_q} : 16'bz;  // Controlled_Buffer controlled_buffer_1
  Multiplexer #(.disabled("Z"), .enable("true"), .width(8)) multiplexer_3 (
    .in0(counter_1_q), .in1(counter_3_q), .out(out_5), .sel(pla_1_out[6]), .en(pla_1_out[5]));
endmodule

module PC_CIRC (
  input  [15:0] in_1,
  input  in_2,
  input  [2:0] in_3,
  output [15:0] out_4,
  output [15:0] out_5
);

  wire and_1_out, and_2_out, and_3_out, counter_1_carry;

  and and_1 (and_1_out, in_3[1], in_3[0]);
  and and_2 (and_2_out, in_3[0], ~in_3[1]);  // AND_Gate
  Counter counter_1 (
    .load(and_2_out), .D(in_1[7:0]), .count(in_3[1]), .Q(out_5[7:0]), .carry(counter_1_carry),
    .up(and_1_out), .clk(in_2));  // open: clr
  and and_3 (and_3_out, counter_1_carry, in_3[1]);
  Counter counter_2 (
    .load(and_2_out), .D(in_1[15:8]), .count(and_3_out), .Q(out_5[15:8]), .up(and_1_out), .clk(in_2));  // open: carry, clr
  assign out_4 = in_3[2] ? out_5 : 16'bz;  // Controlled_Buffer controlled_buffer_1
endmodule

module SP_CIRC (
  input  [15:0] in_1,
  input  in_2,
  input  [2:0] in_3,
  output [15:0] out_4,
  output [15:0] out_5
);

  wire and_1_out, and_2_out, and_3_out, counter_1_carry;

  and and_1 (and_1_out, in_3[1], in_3[0]);
  and and_2 (and_2_out, in_3[0], ~in_3[1]);  // AND_Gate
  Counter counter_1 (
    .load(and_2_out), .D(in_1[7:0]), .count(in_3[1]), .Q(out_5[7:0]), .carry(counter_1_carry),
    .up(and_1_out), .clk(in_2));  // open: clr
  and and_3 (and_3_out, counter_1_carry, in_3[1]);
  Pull_Resistor pull_resistor_1 (.node(out_5[15:13]));
  Counter #(.max('h1f), .width(5)) counter_2 (
    .load(and_2_out), .D(in_1[12:8]), .count(and_3_out), .Q(out_5[12:8]), .up(and_1_out), .clk(in_2));  // open: carry, clr
  assign out_4 = in_3[2] ? out_5 : 16'bz;  // Controlled_Buffer controlled_buffer_1
endmodule

module MM_CIRC (
  input  [15:0] in_1,
  input  [7:0] in_2,
  input  in_3,
  input  [2:0] in_4,
  output [7:0] out_5,
  output [15:0] out_6,
  output [15:0] out_7
);

  wire decoder_1_out1, decoder_1_out2, decoder_1_out3, decoder_1_out5, decoder_1_out6, decoder_1_out7,
       or_1_out, or_2_out, or_3_out;
  wire [7:0] multiplexer_1_out, multiplexer_2_out;

  Decoder #(.enable("false"), .select(3)) decoder_1 (
    .out1(decoder_1_out1), .out2(decoder_1_out2), .out3(decoder_1_out3), .out5(decoder_1_out5),
    .out6(decoder_1_out6), .out7(decoder_1_out7), .sel(in_4));  // open: out0, out4
  Multiplexer #(.width(8)) multiplexer_1 (.in0(in_2), .in1(in_1[7:0]), .out(multiplexer_1_out), .sel(decoder_1_out1));
  or or_1 (or_1_out, decoder_1_out1, decoder_1_out2);
  or or_2 (or_2_out, decoder_1_out1, decoder_1_out3);
  or or_3 (or_3_out, decoder_1_out6, decoder_1_out7);
  Multiplexer #(.width(8)) multiplexer_2 (.in0(in_2), .in1(in_1[15:8]), .out(multiplexer_2_out), .sel(decoder_1_out1));
  Register register_1 (.D(multiplexer_1_out), .en(or_1_out), .Q(out_7[7:0]), .clk(in_3));  // open: clr
  Multiplexer #(.disabled("Z"), .enable("true"), .width(8)) multiplexer_3 (
    .in0(out_7[7:0]), .in1(out_7[15:8]), .out(out_5), .sel(decoder_1_out7), .en(or_3_out));
  Register register_2 (.D(multiplexer_2_out), .en(or_2_out), .Q(out_7[15:8]), .clk(in_3));  // open: clr
  assign out_6 = decoder_1_out5 ? out_7 : 16'bz;  // Controlled_Buffer controlled_buffer_1
endmodule
